# Fritzing sketch schema (saved by Fritzing 1.0.1rc)

parts:
  J1 = Basic Servo
  A2 = VL53lox
  A3 = VL53lox
  J2 = female pin header, 15 pins [form="♀ (female)"]
  J3 = female pin header, 15 pins [form="♀ (female)"]
  J5 = Dagu DGServo 9g header (male) [package=THT]
  A4 = VL53lox
  J6 = female pin header, 1 pin [form="♀ (female)"]
  J7 = female pin header, 1 pin [form="♀ (female)"]
  J8 = female pin header, 2 pins [form="♀ (female)"]
  J9 = female pin header, 2 pins [form="♀ (female)"]
  M1 = DC Motor [voltage_(max)=6V voltage_(min)=3V]
  J10 = female pin header, 1 pin [form="♀ (female)"]
  J11 = female pin header, 1 pin [form="♀ (female)"]
  J12 = female pin header, 1 pin [form="♀ (female)"]
  J13 = female pin header, 1 pin [form="♀ (female)"]
  J14 = female pin header, 1 pin [form="♀ (female)"]
  J15 = female pin header, 1 pin [form="♀ (female)"]
  J16 = female pin header, 7 pins [form="♀ (female)"]
  J17 = female pin header, 6 pins [form="♀ (female)"]
  J18 = female pin header, 6 pins [form="♀ (female)"]
  J19 = female pin header, 3 pins [form="♀ (female)"]

nets:
  N1: J1.gnd, A2.Pin_2, A3.Pin_2, J5.pulse, A4.Pin_2
  VCC: J1.vcc, J5.Vcc
  N2: J1.pulse, J3.pin10
  N3: A2.Pin_1, A3.Pin_1, J3.pin15, A4.Pin_1, J17.pin4
  N4: A2.Pin_3, A3.Pin_3, J3.pin2, A4.Pin_3, J6.pin1
  N5: A2.Pin_4, A3.Pin_4, J3.pin5, A4.Pin_4, J7.pin1
  N6: A2.Pin_6, J3.pin6
  N7: A3.Pin_6, J3.pin7
  N8: J2.pin4, J17.pin1
  N9: J2.pin5, J17.pin2
  N10: J2.pin6, J17.pin5
  N11: J2.pin7, J17.pin6
  N12: J2.pin14, J16.pin1, J17.pin3, J18.pin3
  N13: J2.pin15, J16.pin2, J18.pin4, J19.pin3
  N14: J3.pin11, J19.pin1
  N15: J3.pin13, J5.gnd
  N16: J8.pin1, J15.pin1
  N17: J8.pin2, J12.pin1
  N18: J9.pin1, M1.pin_2
  N19: J9.pin2, M1.pin_1
  N20: J10.pin1, J11.pin1
  N21: J13.pin1, J14.pin1
  N22: J16.pin3, J18.pin1
  N23: J16.pin4, J18.pin2
  N24: J16.pin5, J18.pin5
  N25: J16.pin6, J18.pin6

notes:
  5V
  ECS moteur
  direction
  D15
  D16
  SCL
  SDA
  ESP32, 30 broches
  D19
  D18
  6V
  8V
  Step down
  3.3V
  Batterie 2S
  Arret d'urgence
  Lidar gauche
  Lidar centre
  Lidar droit
  récepteur 433MHz
  convertisseur 5v-3.3v
  Moteur
  D34, 35, 32, 33
  marche arret servo et ECS
  D4
  A3144

custom parts:
  VL53lox: VL53L0X Time-of-Flight (ToF) Laser Ranging Sensor Breakout.
