# Fritzing sketch cablage (saved by Fritzing 1.0.1rc)

parts:
  U1 = Voltage Regulator - 5V [package="TO220 [THT]"]
  VCC1 = Battery
  J1 = Basic Servo
  L1 = Solenoid
  Q1 = Basic FET P-Channel [package="TO220 [THT]"]
  J2 = female pin header, 2 pins [form="♀ (female)"]
  Composant1 = Arduino Nano (Rev3.0)
  R1 = Resistor [tolerance=±5% power=0.25 resistance=10k package=THT]
  S1 = Pushbutton [package=THT]

nets:
  N1: U1.input_voltage, VCC1.+, L1.pin2, Composant1.VIN
  GND: U1.GND, J1.gnd, Q1.drain, S1.leg0
  N2: U1.output_voltage, J1.vcc
  N3: VCC1.-, S1.leg1
  N4: J1.pulse, Composant1.D8
  N5: L1.pin1, Q1.source
  N6: Q1.gate, R1.Pin_0
  N7: J2.pin2, Composant1.GND
  N8: Composant1.D9, R1.Pin_1

notes:
  D9
  2 x 3.6v
  ARU
